# Fritzing sketch BPL_32 (saved by Fritzing 0.9.3b)
circuit board: 5.9953cm x 5.20367cm

parts:
  ROT1 = female pin header, 3 pins [form="♀ (female)"]
  I2C = female pin header, 4 pins [form="♀ (female)"]
  BUZZ = Buzzer 12mm [package=buzzer-12mm]
  4CH_RELAY = female pin header, 6 pins [form="♀ (female)"]
  DOOR = Screw terminal - 2 pins [package=THT]
  5V = Screw terminal - 2 pins [package=THT]
  R1 = Resistor [tolerance=±5% resistance=4.7k package=THT]
  PRESSURE = screw terminal, 3 pins
  OW = screw terminal, 3 pins
  30pin_ESP32 = DOIT Esp32 DevKit v1 (30 pins long, 11 pins width) [part_number=ESP32S-PIN30]

nets:
  N1: ROT1.pin1, 30pin_ESP32.D32
  N2: ROT1.pin2, 30pin_ESP32.D33
  N3: ROT1.pin3, 30pin_ESP32.D25
  GND: I2C.pin1, BUZZ.2, 4CH_RELAY.pin1, DOOR.pin1, 5V.pin1, PRESSURE.pin1, OW.pin1, 30pin_ESP32.GND
  3.3V: I2C.pin2, 30pin_ESP32.3V3
  N4: I2C.pin3, 30pin_ESP32.D21
  N5: I2C.pin4, 30pin_ESP32.D22
  N6: BUZZ.1, 30pin_ESP32.D18
  N7: 4CH_RELAY.pin2, 30pin_ESP32.TX2
  N8: 4CH_RELAY.pin3, 30pin_ESP32.RX2
  N9: 4CH_RELAY.pin4, 30pin_ESP32.D27
  N10: 4CH_RELAY.pin5, 30pin_ESP32.D19
  5V: 4CH_RELAY.pin6, 5V.pin2, R1.Pin_0, PRESSURE.pin3, OW.pin3, 30pin_ESP32.VIN
  N11: DOOR.pin2, 30pin_ESP32.D26
  N12: R1.Pin_1, OW.pin2, 30pin_ESP32.D23
  N13: PRESSURE.pin2, 30pin_ESP32.VP

notes:
  SDA
  SCL
  3.3
  GND
  5V
  GPIO23
  GPIO18
  GPIO17
  GPIO16
  PUSH
  ROTA
  ROTB
  GPIO36
  GPIO27
  heat
  cool
  fan
  spund
  22
  21
  3.3V
  D
  23
  18
  27
  16
  17
  26
  G
  19

custom parts:
  DOIT Esp32 DevKit v1 (30 pins long, 11 pins width): The DOIT Esp32 DevKit v1 is one of the development board created by DOIT to evaluate the ESP-WROOM-32 module. It is based on the ESP32 microcontroller that boasts Wifi, Bluetooth, Ethernet and Low Power support all in a single chip. (vanepp) made breadboard work, adjusted pin numbering and labels and reduced size of schematic and cleaned up pcb. This chip is 30pins long (2 x15) and 11 pins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
